// Logisim project Guia_0401.circ as structural Verilog: 1 circuit, main circuit main
module main (
  input  in_1,
  input  in_2,
  input  in_3,
  input  in_4,
  input  in_5,
  input  in_6,
  input  in_7,
  input  in_8,
  input  in_9,
  input  in_10,
  input  in_11,
  input  in_12,
  input  in_13,
  input  in_14,
  input  in_15,
  input  in_16,
  output out_17,
  output out_18,
  output out_19,
  output out_20,
  output out_21
);

  wire and_1_out, and_2_out, not_1_out, not_2_out, not_3_out, not_4_out, not_5_out, or_1_out, or_2_out,
       or_3_out, or_4_out;

  not not_1 (not_1_out, in_3);
  not not_2 (not_2_out, in_7);
  not not_3 (not_3_out, in_10);
  not not_4 (not_4_out, in_11);
  or or_1 (or_1_out, ~in_2, ~not_1_out);  // OR_Gate
  or or_2 (or_2_out, ~in_4, ~not_5_out);  // OR_Gate
  not not_5 (not_5_out, in_5);
  and and_1 (and_1_out, ~not_2_out, ~in_8);  // AND_Gate
  and and_2 (and_2_out, ~not_3_out, ~not_4_out);  // AND_Gate
  or or_3 (or_3_out, in_13, in_14);
  or or_4 (or_4_out, ~in_15, ~in_16);  // OR_Gate
  and and_3 (out_18, or_2_out, in_6);
  or or_5 (out_19, and_1_out, in_9);
  and and_4 (out_20, and_2_out, in_12);
  and and_5 (out_21, or_3_out, or_4_out);
  and and_6 (out_17, in_1, or_1_out);
endmodule
