// Logisim project Guia_05.circ as structural Verilog: 9 circuits, main circuit main
module main (
  input  A,
  input  B,
  output out_3,
  output out_4,
  output out_5,
  output out_6,
  output out_7,
  output out_8,
  output out_9,
  output out_10
);

  q1_nor q1_nor_1 (.A(A), .B(B), .out_3(out_3));
  q2_nand q2_nand_1 (.A(A), .B(B), .out_3(out_4));
  q3_nor q3_nor_1 (.a(A), .b(B), .out_3(out_5));
  q4_nand q4_nand_1 (.a(A), .b(B), .out_3(out_6));
  q5_nor q5_nor_1 (.a(A), .b(B), .out_3(out_7));
  q6_nand q6_nand_1 (.a(A), .b(B), .out_3(out_8));
  q7_nor q7_nor_1 (.a(A), .b(B), .out_3(out_9));
  q8_nand q8_nand_1 (.a(A), .in_2(B), .out_3(out_10));

  // Notes on the sheet:
  //   1)
  //   2)
  //   3)
  //   4)
  //   5)
  //   6)
  //   7)
  //   8)
endmodule

module q1_nor (
  input  A,
  input  B,
  output out_3
);

  wire nor_1_out;

  nor nor_1 (nor_1_out, B, B);
  nor nor_2 (out_3, A, nor_1_out);
endmodule

module q2_nand (
  input  A,
  input  B,
  output out_3
);

  wire nand_1_out;

  nand nand_1 (nand_1_out, B, B);
  nand nand_2 (out_3, A, nand_1_out);
endmodule

module q3_nor (
  input  a,
  input  b,
  output out_3
);

  wire nor_1_out, nor_2_out;

  nor nor_1 (nor_1_out, a, a);
  nor nor_2 (nor_2_out, nor_1_out, b);
  nor nor_3 (out_3, nor_2_out, nor_2_out);
endmodule

module q4_nand (
  input  a,
  input  b,
  output out_3
);

  wire nand_1_out;

  nand nand_1 (nand_1_out, b, b);
  nand nand_2 (out_3, a, nand_1_out);
endmodule

module q5_nor (
  input  a,
  input  b,
  output out_3
);

  wire nor_1_out, nor_2_out, nor_3_out, nor_4_out;

  nor nor_1 (nor_1_out, a, b);
  nor nor_2 (nor_2_out, a, b);
  nor nor_3 (nor_3_out, a, nor_1_out);
  nor nor_4 (nor_4_out, nor_2_out, b);
  nor nor_5 (out_3, nor_3_out, nor_4_out);
endmodule

module q6_nand (
  input  a,
  input  b,
  output out_3
);

  wire nand_1_out, nand_2_out, nand_3_out, nand_4_out;

  nand nand_1 (nand_1_out, a, b);
  nand nand_2 (nand_2_out, a, b);
  nand nand_3 (nand_3_out, a, nand_1_out);
  nand nand_4 (nand_4_out, nand_2_out, b);
  nand nand_5 (out_3, nand_3_out, nand_4_out);
endmodule

module q7_nor (
  input  a,
  input  b,
  output out_3
);

  wire nor_1_out, nor_2_out, nor_3_out, nor_4_out, nor_5_out;

  nor nor_1 (nor_1_out, a, a);
  nor nor_2 (nor_2_out, b, b);
  nor nor_3 (nor_3_out, nor_1_out, nor_1_out);
  nor nor_4 (nor_4_out, nor_3_out, nor_5_out);
  nor nor_5 (nor_5_out, nor_2_out, nor_2_out);
  nor nor_6 (out_3, nor_4_out, nor_4_out);
endmodule

module q8_nand (
  input  a,
  input  in_2,
  output out_3
);

  wire nand_1_out, nand_2_out;

  nand nand_1 (nand_1_out, a, a);
  nand nand_2 (nand_2_out, in_2, in_2);
  nand nand_3 (out_3, nand_1_out, nand_2_out);
endmodule
