// Logisim project Guia-07-811445-Gabriel_Glatz_Campos.circ as structural Verilog: 6 circuits, main circuit main
module main (
  input  in_1,
  input  in_2,
  input  in_3,
  input  [1:0] in_4,
  input  [2:0] in_5,
  output out_6,
  output out_7,
  output out_8,
  output out_9,
  output out_10
);

  Q01 q01_1 (.in_3(in_3), .in_1(in_1), .in_2(in_2), .out_4(out_6));
  Q02 q02_1 (.in_3(in_3), .in_1(in_1), .in_2(in_2), .out_4(out_7));
  Q03 q03_1 (.in_3(in_4), .A(in_1), .B(in_2), .out_4(out_8));
  Q04 q04_1 (.in_3(in_4), .A(in_1), .B(in_2), .out_4(out_9));
  Q05 q05_1 (.A(in_1), .B(in_2), .in_3(in_5), .out_4(out_10));
endmodule

module Q01 (
  input  in_1,
  input  in_2,
  input  in_3,
  output out_4
);

  wire and_1_out, nand_1_out;

  and and_1 (and_1_out, in_2, in_1);
  nand nand_1 (nand_1_out, in_2, in_1);
  Multiplexer #(.enable("false")) multiplexer_1 (.in0(and_1_out), .in1(nand_1_out), .out(out_4), .sel(in_3));
endmodule

module Q02 (
  input  in_1,
  input  in_2,
  input  in_3,
  output out_4
);

  wire nor_1_out, or_1_out;

  or or_1 (or_1_out, in_2, in_1);
  nor nor_1 (nor_1_out, in_2, in_1);
  Multiplexer #(.enable("false")) multiplexer_1 (.in0(or_1_out), .in1(nor_1_out), .out(out_4), .sel(in_3));
endmodule

module Q03 (
  input  A,
  input  B,
  input  [1:0] in_3,
  output out_4
);

  wire and_2_out, AND_out, multiplexer_2_out, multiplexer_3_out, multiplexer_4_out, nand_2_out, NAND_out,
       nor_2_out, NOR_out, or_2_out, OR_out, undriven, undriven_2, undriven_3;

  or OR (OR_out, B, A);
  nor NOR (NOR_out, B, A);
  and AND (AND_out, B, A);
  nand NAND (NAND_out, B, A);
  Multiplexer #(.select(2), .enable("false")) multiplexer_1 (
    .in0(OR_out), .in1(NOR_out), .in2(AND_out), .in3(NAND_out), .out(out_4), .sel(in_3));
  or or_2 (or_2_out, undriven_2, undriven);
  nor nor_2 (nor_2_out, undriven_2, undriven);
  and and_2 (and_2_out, undriven_2, undriven);
  nand nand_2 (nand_2_out, undriven_2, undriven);
  Multiplexer #(.enable("false")) multiplexer_2 (
    .in0(or_2_out), .in1(nor_2_out), .out(multiplexer_2_out), .sel(undriven_3));
  Multiplexer #(.enable("false")) multiplexer_3 (
    .in0(and_2_out), .in1(nand_2_out), .out(multiplexer_3_out), .sel(undriven_3));
  Multiplexer #(.enable("false")) multiplexer_4 (
    .in0(multiplexer_2_out), .in1(multiplexer_3_out), .out(multiplexer_4_out), .sel(undriven_3));

  // Notes on the sheet:
  //   Exemplo do que ocorre dentro da esquerda
endmodule

module Q04 (
  input  A,
  input  B,
  input  [1:0] in_3,
  output out_4
);

  wire multiplexer_2_out, multiplexer_3_out, multiplexer_4_out, nor_2_out, NOR_out, or_2_out, OR_out,
       undriven, undriven_2, undriven_3, xnor_1_out, xnor_2_out, xor_1_out, xor_2_out;

  or OR (OR_out, B, A);
  nor NOR (NOR_out, B, A);
  xor xor_1 (xor_1_out, B, A);
  xnor xnor_1 (xnor_1_out, B, A);
  Multiplexer #(.select(2), .enable("false")) multiplexer_1 (
    .in0(OR_out), .in1(NOR_out), .in2(xor_1_out), .in3(xnor_1_out), .out(out_4), .sel(in_3));
  or or_2 (or_2_out, undriven_2, undriven);
  nor nor_2 (nor_2_out, undriven_2, undriven);
  xor xor_2 (xor_2_out, undriven_2, undriven);
  xnor xnor_2 (xnor_2_out, undriven_2, undriven);
  Multiplexer #(.enable("false")) multiplexer_2 (
    .in0(or_2_out), .in1(nor_2_out), .out(multiplexer_2_out), .sel(undriven_3));
  Multiplexer #(.enable("false")) multiplexer_3 (
    .in0(xor_2_out), .in1(xnor_2_out), .out(multiplexer_3_out), .sel(undriven_3));
  Multiplexer #(.enable("false")) multiplexer_4 (
    .in0(multiplexer_2_out), .in1(multiplexer_3_out), .out(multiplexer_4_out), .sel(undriven_3));

  // Notes on the sheet:
  //   Exemplo do que ocorre dentro da esquerda
endmodule

module Q05 (
  input  A,
  input  B,
  input  [2:0] in_3,
  output out_4
);

  wire and_1_out, and_2_out, multiplexer_2_out, multiplexer_3_out, multiplexer_4_out, multiplexer_5_out,
       multiplexer_6_out, multiplexer_7_out, multiplexer_8_out, nand_1_out, nand_2_out, nor_1_out, nor_2_out,
       not_1_out, not_2_out, not_3_out, not_4_out, OR_2_out, OR_out, undriven, undriven_2, undriven_3,
       xnor_1_out, xnor_2_out, xor_1_out, xor_2_out;

  not not_1 (not_1_out, B);
  or OR (OR_out, B, A);
  nor nor_1 (nor_1_out, B, A);
  and and_1 (and_1_out, B, A);
  nand nand_1 (nand_1_out, B, A);
  xor xor_1 (xor_1_out, B, A);
  xnor xnor_1 (xnor_1_out, B, A);
  not not_2 (not_2_out, xnor_1_out);
  Multiplexer #(.select(3), .enable("false")) multiplexer_1 (
    .in0(OR_out), .in1(nor_1_out), .in2(and_1_out), .in3(nand_1_out), .in4(xor_1_out), .in5(xnor_1_out),
    .in6(not_1_out), .in7(not_2_out), .out(out_4), .sel(in_3));
  // OR_Gate OR_2 has open pins: out=OR_2_out
  // NOR_Gate nor_2 has open pins: out=nor_2_out
  // AND_Gate and_2 has open pins: out=and_2_out
  // NAND_Gate nand_2 has open pins: out=nand_2_out
  // XOR_Gate xor_2 has open pins: out=xor_2_out
  // XNOR_Gate xnor_2 has open pins: out=xnor_2_out
  // NOT_Gate not_3 has open pins: in=open, out=not_3_out
  not not_4 (not_4_out, xnor_2_out);
  Multiplexer #(.enable("false")) multiplexer_2 (
    .in0(OR_2_out), .in1(nor_2_out), .out(multiplexer_2_out), .sel(undriven));
  Multiplexer #(.enable("false")) multiplexer_3 (
    .in0(multiplexer_2_out), .in1(multiplexer_4_out), .out(multiplexer_3_out), .sel(undriven_2));
  Multiplexer #(.enable("false")) multiplexer_4 (
    .in0(and_2_out), .in1(nand_2_out), .out(multiplexer_4_out), .sel(undriven));
  Multiplexer #(.enable("false")) multiplexer_5 (
    .in0(xor_2_out), .in1(xnor_2_out), .out(multiplexer_5_out), .sel(undriven));
  Multiplexer #(.enable("false")) multiplexer_6 (
    .in0(multiplexer_5_out), .in1(multiplexer_7_out), .out(multiplexer_6_out), .sel(undriven_2));
  Multiplexer #(.enable("false")) multiplexer_7 (
    .in0(not_4_out), .in1(not_3_out), .out(multiplexer_7_out), .sel(undriven));
  Multiplexer #(.enable("false")) multiplexer_8 (
    .in0(multiplexer_3_out), .in1(multiplexer_6_out), .out(multiplexer_8_out), .sel(undriven_3));

  // Notes on the sheet:
  //   Exemplo do que ocorre dentro da esquerda
endmodule
