// Logisim project Guia_08.circ as structural Verilog: 7 circuits, main circuit main
module main (
  input  in_1,
  input  in_2,
  input  in_3,
  input  in_4,
  input  in_5,
  input  in_6,
  input  in_7,
  input  in_8,
  input  in_9,
  input  in_10,
  input  in_11,
  input  in_12,
  input  in_13,
  input  in_14,
  input  in_15,
  input  in_16,
  input  in_17,
  input  in_18,
  input  in_19,
  input  in_20,
  input  in_21,
  input  in_22,
  input  in_23,
  input  in_24,
  input  in_25,
  input  in_26,
  input  in_27,
  input  in_28,
  input  in_29,
  input  in_30,
  input  in_31,
  input  in_32,
  input  in_33,
  input  in_34,
  input  in_35,
  input  in_36,
  input  in_37,
  input  in_38,
  input  in_39,
  input  in_40,
  input  in_41,
  input  in_42,
  input  in_43,
  input  in_44,
  input  in_45,
  output out_46,
  output out_47,
  output out_48,
  output out_49,
  output out_50,
  output out_51,
  output out_52,
  output out_53,
  output out_54,
  output out_55,
  output out_56,
  output out_57,
  output out_58,
  output out_59,
  output out_60,
  output out_61,
  output out_62,
  output out_63,
  output out_64
);

  wire complementode1_1_out_6, complementode1_1_out_7, complementode1_1_out_8, complementode1_1_out_9,
       complementode1_1_out_10, q01_meiasoma_2_s1, q01_meiasoma_3_s1, q01_meiasoma_4_s1, q01_meiasoma_5_s1,
       q02_meiadiferenca_2_s1, q02_meiadiferenca_3_s1, q02_meiadiferenca_4_s1, q02_meiadiferenca_5_s1,
       q03_comparadorigualdade_1_igual, q03_comparadorigualdade_2_p3, q03_comparadorigualdade_2_p5,
       q03_comparadorigualdade_3_igual, q03_comparadorigualdade_4_igual, q03_comparadorigualdade_5_igual,
       q04_comparadordiferenca_1_igual, q04_comparadordiferenca_2_igual, q04_comparadordiferenca_3_igual,
       q04_comparadordiferenca_4_igual, q04_comparadordiferenca_5_igual, q05_somacompleta_2_s1,
       q05_somacompleta_3_s1, q05_somacompleta_4_s1, q05_somacompleta_5_s1;

  Q01_MeiaSoma q01_meiasoma_1 (.A(in_1), .B(in_6), .Vai_Um(q01_meiasoma_2_s1), .S0(out_47), .S1(out_46));
  Q02_MeiaDiferenca q02_meiadiferenca_1 (
    .A(in_11), .B(in_16), .Vem_Um(q02_meiadiferenca_2_s1), .S0(out_53), .S1(out_52));
  Q01_MeiaSoma q01_meiasoma_2 (.A(in_2), .B(in_7), .Vai_Um(q01_meiasoma_3_s1), .S0(out_48), .S1(q01_meiasoma_2_s1));
  Q02_MeiaDiferenca q02_meiadiferenca_2 (
    .A(in_12), .B(in_17), .Vem_Um(q02_meiadiferenca_3_s1), .S0(out_54), .S1(q02_meiadiferenca_2_s1));
  Q03_ComparadorIgualdade q03_comparadorigualdade_1 (
    .A(in_21), .B(in_26), .igual(q03_comparadorigualdade_1_igual));  // open: a_b, a_b_2
  Q04_ComparadorDiferenca q04_comparadordiferenca_1 (
    .A(in_31), .B(in_36), .igual(q04_comparadordiferenca_1_igual));  // open: a_b, a_b_2
  Q05_SomaCompleta q05_somacompleta_1 (
    .A(complementode1_1_out_10), .B(1'b0), .Vai_Um(q05_somacompleta_2_s1), .S0(out_60));  // open: S1
  Q01_MeiaSoma q01_meiasoma_3 (.A(in_3), .B(in_8), .Vai_Um(q01_meiasoma_4_s1), .S0(out_49), .S1(q01_meiasoma_3_s1));
  Q02_MeiaDiferenca q02_meiadiferenca_3 (
    .A(in_13), .B(in_18), .Vem_Um(q02_meiadiferenca_4_s1), .S0(out_55), .S1(q02_meiadiferenca_3_s1));
  // Q03_ComparadorIgualdade q03_comparadorigualdade_2: pin names not known; wires that end beside it: in_28, in_23, q03_comparadorigualdade_2_p3, q03_comparadorigualdade_2_p3, q03_comparadorigualdade_2_p5
  Q03_ComparadorIgualdade q03_comparadorigualdade_3 (
    .A(in_27), .B(in_22), .igual(q03_comparadorigualdade_3_igual));  // open: a_b, a_b_2
  and and_1 (out_58, q03_comparadorigualdade_1_igual, q03_comparadorigualdade_3_igual, q03_comparadorigualdade_2_p5, q03_comparadorigualdade_4_igual, q03_comparadorigualdade_5_igual);
  Q04_ComparadorDiferenca q04_comparadordiferenca_2 (
    .A(in_38), .B(in_33), .igual(q04_comparadordiferenca_2_igual));  // open: a_b, a_b_2
  Q04_ComparadorDiferenca q04_comparadordiferenca_3 (
    .A(in_37), .B(in_32), .igual(q04_comparadordiferenca_3_igual));  // open: a_b, a_b_2
  or or_1 (out_59, q04_comparadordiferenca_1_igual, q04_comparadordiferenca_3_igual, q04_comparadordiferenca_2_igual, q04_comparadordiferenca_4_igual, q04_comparadordiferenca_5_igual);
  ComplementoDe1 complementode1_1 (
    .in_1(in_45), .in_2(in_44), .in_3(in_43), .in_4(in_42), .in_5(in_41), .out_6(complementode1_1_out_6),
    .out_7(complementode1_1_out_7), .out_8(complementode1_1_out_8), .out_9(complementode1_1_out_9),
    .out_10(complementode1_1_out_10));
  Q05_SomaCompleta q05_somacompleta_2 (
    .A(complementode1_1_out_9), .B(1'b0), .Vai_Um(q05_somacompleta_3_s1), .S0(out_61),
    .S1(q05_somacompleta_2_s1));
  Q01_MeiaSoma q01_meiasoma_4 (.A(in_4), .B(in_9), .Vai_Um(q01_meiasoma_5_s1), .S0(out_50), .S1(q01_meiasoma_4_s1));
  Q02_MeiaDiferenca q02_meiadiferenca_4 (
    .A(in_14), .B(in_19), .Vem_Um(q02_meiadiferenca_5_s1), .S0(out_56), .S1(q02_meiadiferenca_4_s1));
  Q03_ComparadorIgualdade q03_comparadorigualdade_4 (
    .A(in_29), .B(in_24), .igual(q03_comparadorigualdade_4_igual));  // open: a_b, a_b_2
  Q04_ComparadorDiferenca q04_comparadordiferenca_4 (
    .A(in_39), .B(in_34), .igual(q04_comparadordiferenca_4_igual));  // open: a_b, a_b_2
  Q05_SomaCompleta q05_somacompleta_3 (
    .A(complementode1_1_out_8), .B(1'b0), .Vai_Um(q05_somacompleta_4_s1), .S0(out_62),
    .S1(q05_somacompleta_3_s1));
  Q01_MeiaSoma q01_meiasoma_5 (.A(in_5), .B(in_10), .Vai_Um(1'b0), .S0(out_51), .S1(q01_meiasoma_5_s1));
  Q02_MeiaDiferenca q02_meiadiferenca_5 (.A(in_15), .B(in_20), .Vem_Um(1'b0), .S0(out_57), .S1(q02_meiadiferenca_5_s1));
  Q03_ComparadorIgualdade q03_comparadorigualdade_5 (
    .A(in_30), .B(in_25), .igual(q03_comparadorigualdade_5_igual));  // open: a_b, a_b_2
  Q04_ComparadorDiferenca q04_comparadordiferenca_5 (
    .A(in_40), .B(in_35), .igual(q04_comparadordiferenca_5_igual));  // open: a_b, a_b_2
  Q05_SomaCompleta q05_somacompleta_4 (
    .A(complementode1_1_out_7), .B(1'b0), .Vai_Um(q05_somacompleta_5_s1), .S0(out_63),
    .S1(q05_somacompleta_4_s1));
  Q05_SomaCompleta q05_somacompleta_5 (
    .A(complementode1_1_out_6), .B(1'b1), .Vai_Um(1'b0), .S0(out_64), .S1(q05_somacompleta_5_s1));

  // Notes on the sheet:
  //   Q01)
  //   Q02)
  //   Q03)
  //   Q04)
  //   Q05)
endmodule

module Q01_MeiaSoma (
  input  A,
  input  B,
  input  Vai_Um,
  output S0,
  output S1
);

  wire and_1_out, and_2_out, xor_1_out;

  xor xor_1 (xor_1_out, A, B);
  and and_1 (and_1_out, B, A);
  xor xor_2 (S0, Vai_Um, xor_1_out);
  and and_2 (and_2_out, xor_1_out, Vai_Um);
  or or_1 (S1, and_2_out, and_1_out);
endmodule

module Q02_MeiaDiferenca (
  input  A,
  input  B,
  input  Vem_Um,
  output S0,
  output S1
);

  wire and_1_out, and_2_out, not_1_out, not_2_out, xor_1_out;

  xor xor_1 (xor_1_out, A, B);
  and and_1 (and_1_out, B, not_1_out);
  not not_1 (not_1_out, A);
  xor xor_2 (S0, Vem_Um, xor_1_out);
  and and_2 (and_2_out, Vem_Um, not_2_out);
  not not_2 (not_2_out, xor_1_out);
  or or_1 (S1, and_2_out, and_1_out);
endmodule

module Q03_ComparadorIgualdade (
  input  A,
  input  B,
  output a_b,
  output igual,
  output a_b_2
);

  wire not_1_out, not_2_out;

  not not_1 (not_1_out, A);
  not not_2 (not_2_out, B);
  and and_1 (a_b, not_1_out, B);
  xnor xnor_1 (igual, A, B);
  and and_2 (a_b_2, A, not_2_out);
endmodule

module Q04_ComparadorDiferenca (
  input  A,
  input  B,
  output a_b,
  output igual,
  output a_b_2
);

  wire not_1_out, not_2_out;

  not not_1 (not_1_out, A);
  not not_2 (not_2_out, B);
  and and_1 (a_b, not_1_out, B);
  xor xor_1 (igual, A, B);
  and and_2 (a_b_2, A, not_2_out);
endmodule

module Q05_SomaCompleta (
  input  A,
  input  B,
  input  Vai_Um,
  output S0,
  output S1
);

  wire and_1_out, and_2_out, xor_1_out;

  xor xor_1 (xor_1_out, A, B);
  and and_1 (and_1_out, B, A);
  xor xor_2 (S0, Vai_Um, xor_1_out);
  and and_2 (and_2_out, xor_1_out, Vai_Um);
  or or_1 (S1, and_2_out, and_1_out);
endmodule

module ComplementoDe1 (
  input  in_1,
  input  in_2,
  input  in_3,
  input  in_4,
  input  in_5,
  output out_6,
  output out_7,
  output out_8,
  output out_9,
  output out_10
);

  not not_1 (out_6, in_1);
  not not_2 (out_7, in_2);
  not not_3 (out_8, in_3);
  not not_4 (out_9, in_4);
  not not_5 (out_10, in_5);
endmodule
